# Fritzing sketch pinconnections (saved by Fritzing 0.9.3b)

parts:
  Raspberry_Pi_1 = Raspberry Pi 3 [part_number=RPI-3-V1.2]
  Parça1 = NRF24L01+ Breakout Board
  Parça4 = NRF24L01+ Breakout Board
  Parça3 = Arduino Uno (Rev3)

nets:
  3V3: Raspberry_Pi_1.3v3, Parça1.VCC
  N1: Raspberry_Pi_1.GPIO10, Parça1.MOSI
  N2: Raspberry_Pi_1.GPIO9, Parça1.MISO
  N3: Raspberry_Pi_1.GPIO11, Raspberry_Pi_1.GPIO13, Parça1.SCK
  N4: Raspberry_Pi_1.GPIO8, Parça1.CS
  N5: Raspberry_Pi_1.GPIO25, Parça1.CE
  GND: Raspberry_Pi_1.GND, Parça1.GND
  GND_2: Parça4.GND, Parça3.GND
  VCC: Parça4.VCC, Parça3.3V3
  N6: Parça4.CE, Parça3.D9_PWM
  N7: Parça4.CS, Parça3.D10_PWM/SS
  N8: Parça4.SCK, Parça3.D13/SCK
  N9: Parça4.MOSI, Parça3.D11_PWM/MOSI
  N10: Parça4.MISO, Parça3.D12/MISO
